// Logisim project ALU32.circ as structural Verilog: 12 circuits, main circuit ALU1
module ALU1 (
  input  Ainvert,
  input  A,
  input  B,
  input  Less,
  input  Cin,
  input  Binvert,
  input  [1:0] Operation,
  output Result,
  output Cout
);

  wire and_1_out, fulladder_1_s, multiplexer_1_out, multiplexer_2_out, not_1_out, not_2_out, or_1_out;

  not not_1 (not_1_out, A);
  not not_2 (not_2_out, B);
  Multiplexer multiplexer_1 (.in0(A), .in1(not_1_out), .out(multiplexer_1_out), .sel(Ainvert));
  Multiplexer multiplexer_2 (.in0(B), .in1(not_2_out), .out(multiplexer_2_out), .sel(Binvert));
  and and_1 (and_1_out, multiplexer_1_out, multiplexer_2_out);
  or or_1 (or_1_out, multiplexer_1_out, multiplexer_2_out);
  FullAdder fulladder_1 (.A(multiplexer_1_out), .B(multiplexer_2_out), .Cin(Cin), .S(fulladder_1_s), .Cout(Cout));
  Multiplexer #(.select(2)) multiplexer_3 (
    .in0(and_1_out), .in1(or_1_out), .in2(fulladder_1_s), .in3(Less), .out(Result), .sel(Operation));
endmodule

module FullAdder (
  input  A,
  input  B,
  input  Cin,
  output S,
  output Cout
);

  wire and_1_out, and_2_out, or_1_out, xor_1_out;

  xor xor_1 (xor_1_out, A, B);
  and and_1 (and_1_out, B, A);
  or or_1 (or_1_out, B, A);
  xor xor_2 (S, xor_1_out, Cin);
  and and_2 (and_2_out, or_1_out, Cin);
  or or_2 (Cout, and_1_out, and_2_out);
endmodule

module ALU32bits (
  input  [31:0] B,
  input  [31:0] A,
  input  [3:0] ALUOperation,
  output ZERO,
  output [31:0] out_5
);

  wire alu1_1_cout, alu1_2_cout, alu1_3_cout, alu1_4_cout, alu1_5_cout, alu1_6_cout, alu1_7_cout,
       alu1_8_cout, alu1_9_cout, alu1_10_cout, alu1_11_cout, alu1_12_cout, alu1_13_cout, alu1_14_cout,
       alu1_15_cout, alu1_16_cout, alu1_17_cout, alu1_18_cout, alu1_19_cout, alu1_20_cout, alu1_21_cout,
       alu1_22_cout, alu1_23_cout, alu1_24_cout, alu1_25_cout, alu1_26_cout, alu1_27_cout, alu1_28_cout,
       alu1_29_cout, alu1_30_cout, alu1_31_cout, alu1msb_1_set, or_1_out;

  ALU1 alu1_1 (
    .Ainvert(ALUOperation[3]), .A(A[0]), .B(B[0]), .Less(alu1msb_1_set), .Cin(ALUOperation[2]),
    .Binvert(ALUOperation[2]), .Operation(ALUOperation[1:0]), .Result(out_5[0]), .Cout(alu1_1_cout));
  ALU1 alu1_2 (
    .Ainvert(ALUOperation[3]), .A(A[1]), .B(B[1]), .Less(1'b0), .Cin(alu1_1_cout), .Binvert(ALUOperation[2]),
    .Operation(ALUOperation[1:0]), .Result(out_5[1]), .Cout(alu1_2_cout));
  ALU1 alu1_3 (
    .Ainvert(ALUOperation[3]), .A(A[2]), .B(B[2]), .Less(1'b0), .Cin(alu1_2_cout), .Binvert(ALUOperation[2]),
    .Operation(ALUOperation[1:0]), .Result(out_5[2]), .Cout(alu1_3_cout));
  ALU1 alu1_4 (
    .Ainvert(ALUOperation[3]), .A(A[3]), .B(B[3]), .Less(1'b0), .Cin(alu1_3_cout), .Binvert(ALUOperation[2]),
    .Operation(ALUOperation[1:0]), .Result(out_5[3]), .Cout(alu1_4_cout));
  ALU1 alu1_5 (
    .Ainvert(ALUOperation[3]), .A(A[4]), .B(B[4]), .Less(1'b0), .Cin(alu1_4_cout), .Binvert(ALUOperation[2]),
    .Operation(ALUOperation[1:0]), .Result(out_5[4]), .Cout(alu1_5_cout));
  ALU1 alu1_6 (
    .Ainvert(ALUOperation[3]), .A(A[5]), .B(B[5]), .Less(1'b0), .Cin(alu1_5_cout), .Binvert(ALUOperation[2]),
    .Operation(ALUOperation[1:0]), .Result(out_5[5]), .Cout(alu1_6_cout));
  ALU1 alu1_7 (
    .Ainvert(ALUOperation[3]), .A(A[6]), .B(B[6]), .Less(1'b0), .Cin(alu1_6_cout), .Binvert(ALUOperation[2]),
    .Operation(ALUOperation[1:0]), .Result(out_5[6]), .Cout(alu1_7_cout));
  ALU1 alu1_8 (
    .Ainvert(ALUOperation[3]), .A(A[7]), .B(B[7]), .Less(1'b0), .Cin(alu1_7_cout), .Binvert(ALUOperation[2]),
    .Operation(ALUOperation[1:0]), .Result(out_5[7]), .Cout(alu1_8_cout));
  ALU1 alu1_9 (
    .Ainvert(ALUOperation[3]), .A(A[8]), .B(B[8]), .Less(1'b0), .Cin(alu1_8_cout), .Binvert(ALUOperation[2]),
    .Operation(ALUOperation[1:0]), .Result(out_5[8]), .Cout(alu1_9_cout));
  ALU1 alu1_10 (
    .Ainvert(ALUOperation[3]), .A(A[9]), .B(B[9]), .Less(1'b0), .Cin(alu1_9_cout), .Binvert(ALUOperation[2]),
    .Operation(ALUOperation[1:0]), .Result(out_5[9]), .Cout(alu1_10_cout));
  ALU1 alu1_11 (
    .Ainvert(ALUOperation[3]), .A(A[10]), .B(B[10]), .Less(1'b0), .Cin(alu1_10_cout),
    .Binvert(ALUOperation[2]), .Operation(ALUOperation[1:0]), .Result(out_5[10]), .Cout(alu1_11_cout));
  ALU1 alu1_12 (
    .Ainvert(ALUOperation[3]), .A(A[11]), .B(B[11]), .Less(1'b0), .Cin(alu1_11_cout),
    .Binvert(ALUOperation[2]), .Operation(ALUOperation[1:0]), .Result(out_5[11]), .Cout(alu1_12_cout));
  ALU1 alu1_13 (
    .Ainvert(ALUOperation[3]), .A(A[12]), .B(B[12]), .Less(1'b0), .Cin(alu1_12_cout),
    .Binvert(ALUOperation[2]), .Operation(ALUOperation[1:0]), .Result(out_5[12]), .Cout(alu1_13_cout));
  ALU1 alu1_14 (
    .Ainvert(ALUOperation[3]), .A(A[13]), .B(B[13]), .Less(1'b0), .Cin(alu1_13_cout),
    .Binvert(ALUOperation[2]), .Operation(ALUOperation[1:0]), .Result(out_5[13]), .Cout(alu1_14_cout));
  ALU1 alu1_15 (
    .Ainvert(ALUOperation[3]), .A(A[14]), .B(B[14]), .Less(1'b0), .Cin(alu1_14_cout),
    .Binvert(ALUOperation[2]), .Operation(ALUOperation[1:0]), .Result(out_5[14]), .Cout(alu1_15_cout));
  ALU1 alu1_16 (
    .Ainvert(ALUOperation[3]), .A(A[15]), .B(B[15]), .Less(1'b0), .Cin(alu1_15_cout),
    .Binvert(ALUOperation[2]), .Operation(ALUOperation[1:0]), .Result(out_5[15]), .Cout(alu1_16_cout));
  ALU1 alu1_17 (
    .Ainvert(ALUOperation[3]), .A(A[16]), .B(B[16]), .Less(1'b0), .Cin(alu1_16_cout),
    .Binvert(ALUOperation[2]), .Operation(ALUOperation[1:0]), .Result(out_5[16]), .Cout(alu1_17_cout));
  ALU1 alu1_18 (
    .Ainvert(ALUOperation[3]), .A(A[17]), .B(B[17]), .Less(1'b0), .Cin(alu1_17_cout),
    .Binvert(ALUOperation[2]), .Operation(ALUOperation[1:0]), .Result(out_5[17]), .Cout(alu1_18_cout));
  ALU1 alu1_19 (
    .Ainvert(ALUOperation[3]), .A(A[18]), .B(B[18]), .Less(1'b0), .Cin(alu1_18_cout),
    .Binvert(ALUOperation[2]), .Operation(ALUOperation[1:0]), .Result(out_5[18]), .Cout(alu1_19_cout));
  ALU1 alu1_20 (
    .Ainvert(ALUOperation[3]), .A(A[19]), .B(B[19]), .Less(1'b0), .Cin(alu1_19_cout),
    .Binvert(ALUOperation[2]), .Operation(ALUOperation[1:0]), .Result(out_5[19]), .Cout(alu1_20_cout));
  ALU1 alu1_21 (
    .Ainvert(ALUOperation[3]), .A(A[20]), .B(B[20]), .Less(1'b0), .Cin(alu1_20_cout),
    .Binvert(ALUOperation[2]), .Operation(ALUOperation[1:0]), .Result(out_5[20]), .Cout(alu1_21_cout));
  ALU1 alu1_22 (
    .Ainvert(ALUOperation[3]), .A(A[21]), .B(B[21]), .Less(1'b0), .Cin(alu1_21_cout),
    .Binvert(ALUOperation[2]), .Operation(ALUOperation[1:0]), .Result(out_5[21]), .Cout(alu1_22_cout));
  ALU1 alu1_23 (
    .Ainvert(ALUOperation[3]), .A(A[22]), .B(B[22]), .Less(1'b0), .Cin(alu1_22_cout),
    .Binvert(ALUOperation[2]), .Operation(ALUOperation[1:0]), .Result(out_5[22]), .Cout(alu1_23_cout));
  ALU1 alu1_24 (
    .Ainvert(ALUOperation[3]), .A(A[23]), .B(B[23]), .Less(1'b0), .Cin(alu1_23_cout),
    .Binvert(ALUOperation[2]), .Operation(ALUOperation[1:0]), .Result(out_5[23]), .Cout(alu1_24_cout));
  ALU1 alu1_25 (
    .Ainvert(ALUOperation[3]), .A(A[24]), .B(B[24]), .Less(1'b0), .Cin(alu1_24_cout),
    .Binvert(ALUOperation[2]), .Operation(ALUOperation[1:0]), .Result(out_5[24]), .Cout(alu1_25_cout));
  ALU1 alu1_26 (
    .Ainvert(ALUOperation[3]), .A(A[25]), .B(B[25]), .Less(1'b0), .Cin(alu1_25_cout),
    .Binvert(ALUOperation[2]), .Operation(ALUOperation[1:0]), .Result(out_5[25]), .Cout(alu1_26_cout));
  ALU1 alu1_27 (
    .Ainvert(ALUOperation[3]), .A(A[26]), .B(B[26]), .Less(1'b0), .Cin(alu1_26_cout),
    .Binvert(ALUOperation[2]), .Operation(ALUOperation[1:0]), .Result(out_5[26]), .Cout(alu1_27_cout));
  ALU1 alu1_28 (
    .Ainvert(ALUOperation[3]), .A(A[27]), .B(B[27]), .Less(1'b0), .Cin(alu1_27_cout),
    .Binvert(ALUOperation[2]), .Operation(ALUOperation[1:0]), .Result(out_5[27]), .Cout(alu1_28_cout));
  ALU1 alu1_29 (
    .Ainvert(ALUOperation[3]), .A(A[28]), .B(B[28]), .Less(1'b0), .Cin(alu1_28_cout),
    .Binvert(ALUOperation[2]), .Operation(ALUOperation[1:0]), .Result(out_5[28]), .Cout(alu1_29_cout));
  ALU1 alu1_30 (
    .Ainvert(ALUOperation[3]), .A(A[29]), .B(B[29]), .Less(1'b0), .Cin(alu1_29_cout),
    .Binvert(ALUOperation[2]), .Operation(ALUOperation[1:0]), .Result(out_5[29]), .Cout(alu1_30_cout));
  ALU1 alu1_31 (
    .Ainvert(ALUOperation[3]), .A(A[30]), .B(B[30]), .Less(1'b0), .Cin(alu1_30_cout),
    .Binvert(ALUOperation[2]), .Operation(ALUOperation[1:0]), .Result(out_5[30]), .Cout(alu1_31_cout));
  ALU1MSB alu1msb_1 (
    .Ainvert(ALUOperation[3]), .A(A[31]), .B(B[31]), .Less(1'b0), .Binvert(ALUOperation[2]),
    .Cin(alu1_31_cout), .Operation(ALUOperation[1:0]), .Result(out_5[31]), .Set(alu1msb_1_set));  // open: Cout
  or or_1 (or_1_out, out_5[0], out_5[1], out_5[2], out_5[3], out_5[4], out_5[5], out_5[6], out_5[7], out_5[8], out_5[9], out_5[10], out_5[11], out_5[12], out_5[13], out_5[14], out_5[15], out_5[16], out_5[17], out_5[18], out_5[19], out_5[20], out_5[21], out_5[22], out_5[23], out_5[24], out_5[25], out_5[26], out_5[27], out_5[28], out_5[29], out_5[30], out_5[31]);
  not not_1 (ZERO, or_1_out);

  // Other names for the same wires on the sheet: A00 = A[0]; A01 = A[1]; A02 = A[2]; A03 = A[3]; A04 = A[4];
  //   A05 = A[5]; A06 = A[6]; A07 = A[7]; A08 = A[8]; A09 = A[9]; OPERATION[1:0] = ALUOperation[1:0];
  //   Binvert = ALUOperation[2]; Ainvert = ALUOperation[3]; B00 = B[0]; B01 = B[1]; B02 = B[2]; B03 = B[3];
  //   B04 = B[4]; B05 = B[5]; B06 = B[6]; B07 = B[7]; B08 = B[8]; B09 = B[9]; R1 = out_5[0]; R2 = out_5[1];
  //   R3 = out_5[2]; R4 = out_5[3]; R5 = out_5[4]; R6 = out_5[5]; R7 = out_5[6]; R8 = out_5[7]; R9 = out_5[8];
  //   R10 = out_5[9]; R11 = out_5[10]; R12 = out_5[11]; R13 = out_5[12]; R14 = out_5[13]; R15 = out_5[14];
  //   R16 = out_5[15]; R17 = out_5[16]; R18 = out_5[17]; R19 = out_5[18]; R20 = out_5[19]; R21 = out_5[20];
  //   R22 = out_5[21]; R23 = out_5[22]; R24 = out_5[23]; R25 = out_5[24]; R26 = out_5[25]; R27 = out_5[26];
  //   R28 = out_5[27]; R29 = out_5[28]; R30 = out_5[29]; R31 = out_5[30]; R32 = out_5[31]
endmodule

module ALU1MSB (
  input  Ainvert,
  input  A,
  input  B,
  input  Less,
  input  Binvert,
  input  Cin,
  input  [1:0] Operation,
  output Result,
  output Cout,
  output Set
);

  wire and_1_out, fulladder_1_s, multiplexer_1_out, multiplexer_2_out, not_1_out, not_2_out, or_1_out,
       xor_1_out;

  not not_1 (not_1_out, A);
  not not_2 (not_2_out, B);
  Multiplexer multiplexer_1 (.in0(A), .in1(not_1_out), .out(multiplexer_1_out), .sel(Ainvert));
  Multiplexer multiplexer_2 (.in0(B), .in1(not_2_out), .out(multiplexer_2_out), .sel(Binvert));
  and and_1 (and_1_out, multiplexer_1_out, multiplexer_2_out);
  or or_1 (or_1_out, multiplexer_1_out, multiplexer_2_out);
  FullAdder fulladder_1 (.A(multiplexer_1_out), .B(multiplexer_2_out), .Cin(Cin), .S(fulladder_1_s), .Cout(Cout));
  Multiplexer #(.select(2)) multiplexer_3 (
    .in0(and_1_out), .in1(or_1_out), .in2(fulladder_1_s), .in3(Less), .out(Result), .sel(Operation));
  xor xor_1 (xor_1_out, Cout, Cin);
  xor xor_2 (Set, fulladder_1_s, xor_1_out);
endmodule

module register_bank (
  input  Clock,
  input  Reset,
  input  [31:0] Write_data,
  input  [4:0] Bit_register_1,
  input  [4:0] Bit_register_2,
  input  [4:0] Write_register,
  input  enable_write,
  output [31:0] ReadData1,
  output [31:0] ReadData2
);

  wire E0, E1, E2, E3, E4, E5, E6, E7, E8, E9, E10, E11, E12, E13, E14, E15, E16, E17, E18, E19, E20, E21,
       E22, E23, E24, E25, E26, E27, E28, E29, E30, E31;
  wire [31:0] Q0, Q1, Q2, Q3, Q4, Q5, Q6, Q7, Q8, Q9, Q10, Q11, Q12, Q13, Q14, Q15, Q16, Q17, Q18, Q19, Q20,
       Q21, Q22, Q23, Q24, Q25, Q26, Q27, Q28, Q29, Q30, Q31;

  Decoder #(.select(5)) decoder_1 (
    .out0(E0), .out1(E1), .out2(E2), .out3(E3), .out4(E4), .out5(E5), .out6(E6), .out7(E7), .out8(E8),
    .out9(E9), .out10(E10), .out11(E11), .out12(E12), .out13(E13), .out14(E14), .out15(E15), .out16(E16),
    .out17(E17), .out18(E18), .out19(E19), .out20(E20), .out21(E21), .out22(E22), .out23(E23), .out24(E24),
    .out25(E25), .out26(E26), .out27(E27), .out28(E28), .out29(E29), .out30(E30), .out31(E31),
    .sel(Write_register), .en(enable_write));
  Register #(.width(32)) zero (.D({32{1'b0}}), .en(E0), .clk(Clock), .Q(Q0), .clr(Reset));
  Register #(.width(32)) at (.D(Write_data), .en(E1), .clk(Clock), .Q(Q1), .clr(Reset));
  Register #(.width(32)) v0 (.D(Write_data), .en(E2), .clk(Clock), .Q(Q2), .clr(Reset));
  Register #(.width(32)) v1 (.D(Write_data), .en(E3), .clk(Clock), .Q(Q3), .clr(Reset));
  Register #(.width(32)) a0 (.D(Write_data), .en(E4), .clk(Clock), .Q(Q4), .clr(Reset));
  Register #(.width(32)) a1 (.D(Write_data), .en(E5), .clk(Clock), .Q(Q5), .clr(Reset));
  Register #(.width(32)) a2 (.D(Write_data), .en(E6), .clk(Clock), .Q(Q6), .clr(Reset));
  Register #(.width(32)) a3 (.D(Write_data), .en(E7), .clk(Clock), .Q(Q7), .clr(Reset));
  Register #(.width(32)) t0 (.D(Write_data), .en(E8), .clk(Clock), .Q(Q8), .clr(Reset));
  Register #(.width(32)) t1 (.D(Write_data), .en(E9), .clk(Clock), .Q(Q9), .clr(Reset));
  Register #(.width(32)) t2 (.D(Write_data), .en(E10), .clk(Clock), .Q(Q10), .clr(Reset));
  Register #(.width(32)) t3 (.D(Write_data), .en(E11), .clk(Clock), .Q(Q11), .clr(Reset));
  Register #(.width(32)) t4 (.D(Write_data), .en(E12), .clk(Clock), .Q(Q12), .clr(Reset));
  Register #(.width(32)) t5 (.D(Write_data), .en(E13), .clk(Clock), .Q(Q13), .clr(Reset));
  Register #(.width(32)) t6 (.D(Write_data), .en(E14), .clk(Clock), .Q(Q14), .clr(Reset));
  Register #(.width(32)) t7 (.D(Write_data), .en(E15), .clk(Clock), .Q(Q15), .clr(Reset));
  Register #(.width(32)) s0 (.D(Write_data), .en(E16), .clk(Clock), .Q(Q16), .clr(Reset));
  Register #(.width(32)) s1 (.D(Write_data), .en(E17), .clk(Clock), .Q(Q17), .clr(Reset));
  Register #(.width(32)) s2 (.D(Write_data), .en(E18), .clk(Clock), .Q(Q18), .clr(Reset));
  Register #(.width(32)) s3 (.D(Write_data), .en(E19), .clk(Clock), .Q(Q19), .clr(Reset));
  Register #(.width(32)) s4 (.D(Write_data), .en(E20), .clk(Clock), .Q(Q20), .clr(Reset));
  Register #(.width(32)) s5 (.D(Write_data), .en(E21), .clk(Clock), .Q(Q21), .clr(Reset));
  Register #(.width(32)) s6 (.D(Write_data), .en(E22), .clk(Clock), .Q(Q22), .clr(Reset));
  Register #(.width(32)) s7 (.D(Write_data), .en(E23), .clk(Clock), .Q(Q23), .clr(Reset));
  Register #(.width(32)) t8 (.D(Write_data), .en(E24), .clk(Clock), .Q(Q24), .clr(Reset));
  Register #(.width(32)) t9 (.D(Write_data), .en(E25), .clk(Clock), .Q(Q25), .clr(Reset));
  Register #(.width(32)) k0 (.D(Write_data), .en(E26), .clk(Clock), .Q(Q26), .clr(Reset));
  Register #(.width(32)) k1 (.D(Write_data), .en(E27), .clk(Clock), .Q(Q27), .clr(Reset));
  Register #(.width(32)) gp (.D(Write_data), .en(E28), .clk(Clock), .Q(Q28), .clr(Reset));
  Register #(.width(32)) sp (.D(Write_data), .en(E29), .clk(Clock), .Q(Q29), .clr(Reset));
  Register #(.width(32)) fp (.D(Write_data), .en(E30), .clk(Clock), .Q(Q30), .clr(Reset));
  Register #(.width(32)) ra (.D(Write_data), .en(E31), .clk(Clock), .Q(Q31), .clr(Reset));
  Multiplexer #(.select(5), .width(32)) multiplexer_1 (
    .in0(Q0), .in1(Q1), .in2(Q2), .in3(Q3), .in4(Q4), .in5(Q5), .in6(Q6), .in7(Q7), .in8(Q8), .in9(Q9),
    .in10(Q10), .in11(Q11), .in12(Q12), .in13(Q13), .in14(Q14), .in15(Q15), .in16(Q16), .in17(Q17),
    .in18(Q18), .in19(Q19), .in20(Q20), .in21(Q21), .in22(Q22), .in23(Q23), .in24(Q24), .in25(Q25),
    .in26(Q26), .in27(Q27), .in28(Q28), .in29(Q29), .in30(Q30), .in31(Q31), .out(ReadData1),
    .sel(Bit_register_1));
  Multiplexer #(.select(5), .width(32)) multiplexer_2 (
    .in0(Q0), .in1(Q1), .in2(Q2), .in3(Q3), .in4(Q4), .in5(Q5), .in6(Q6), .in7(Q7), .in8(Q8), .in9(Q9),
    .in10(Q10), .in11(Q11), .in12(Q12), .in13(Q13), .in14(Q14), .in15(Q15), .in16(Q16), .in17(Q17),
    .in18(Q18), .in19(Q19), .in20(Q20), .in21(Q21), .in22(Q22), .in23(Q23), .in24(Q24), .in25(Q25),
    .in26(Q26), .in27(Q27), .in28(Q28), .in29(Q29), .in30(Q30), .in31(Q31), .out(ReadData2),
    .sel(Bit_register_2));

  // Other names for the same wires on the sheet: clock_signal = Clock; reset_signal = Reset;
  //   writen_data[31:0] = Write_data
endmodule

module intruction_format (
  input  [31:0] Instruction,
  output [5:0] Op_code,
  output [4:0] rs,
  output [4:0] rt,
  output [4:0] rd,
  output [4:0] shamt,
  output [5:0] funct,
  output [15:0] inmediate,
  output [25:0] address
);


  assign address = Instruction[25:0];
  assign funct = Instruction[5:0];
  assign inmediate = Instruction[15:0];
  assign Op_code = Instruction[31:26];
  assign rd = Instruction[15:11];
  assign rs = Instruction[25:21];
  assign rt = Instruction[20:16];
  assign shamt = Instruction[10:6];

  // Other names for the same wires on the sheet: immediate[15:0] = Instruction[15:0];
  //   shift_amount[4:0] = Instruction[10:6]
endmodule

module DataMemory (
  input  [31:0] Address,
  input  mem_write,
  input  mem_read,
  input  Clock_rate,
  input  [31:0] Written_data,
  output [31:0] Read_data
);

  RAM #(.asyncread("true"), .clearpin("true"), .dataWidth(32)) ram_1 (
    .addr(Address[9:2]), .we(mem_write), .oe(mem_read), .clk(Clock_rate), .din(Written_data), .dout(Read_data));  // open: clr

  // Other names for the same wires on the sheet: MemoryAdress[7:0] = Address[9:2]
endmodule

// OpCode
module controller (
  input  [5:0] OpCode,
  output ALUsource,
  output RegDestino,
  output Jump,
  output Branch,
  output MemRead,
  output MemToReg,
  output MemWrite,
  output RegWrite,
  output [1:0] ALUoperation,
  output LoadByte
);

  wire EsAddI, EsLw;

  Comparator #(.width(6)) comparator_1 (.a({6{1'b0}}), .b(OpCode), .eq(ALUoperation[1]));  // open: gt, lt
  Comparator #(.width(6)) comparator_2 (.a(6'b000010), .b(OpCode), .eq(Jump));  // open: gt, lt
  Comparator #(.width(6)) comparator_3 (.a(6'b000100), .b(OpCode), .eq(ALUoperation[0]));  // open: gt, lt
  Comparator #(.width(6)) comparator_4 (.a(6'b100011), .b(OpCode), .eq(EsLw));  // open: gt, lt
  Comparator #(.width(6)) comparator_5 (.a(6'b101011), .b(OpCode), .eq(MemWrite));  // open: gt, lt
  Comparator #(.width(6)) comparator_6 (.a(6'b001000), .b(OpCode), .eq(EsAddI));  // open: gt, lt
  Comparator #(.width(6)) comparator_7 (.a(6'b100000), .b(OpCode), .eq(LoadByte));  // open: gt, lt
  or or_1 (MemToReg, EsLw, LoadByte);
  or or_2 (MemRead, EsLw, LoadByte);
  or or_3 (RegWrite, EsAddI, ALUoperation[1], EsLw, LoadByte);
  or or_4 (ALUsource, EsAddI, EsLw, MemWrite, LoadByte);

  assign Branch = ALUoperation[0];
  assign RegDestino = ALUoperation[1];

  // Other names for the same wires on the sheet: ALUopOne = ALUoperation[0]; B = ALUoperation[0];
  //   ALUopTwo = ALUoperation[1]; R = ALUoperation[1]; EsLb = LoadByte; J = Jump; MRead = MemRead; MToReg = MemToReg;
  //   MW = MemWrite; RW = RegWrite

  // Notes on the sheet:
  //   Formato R
  //   J
  //   Beq
  //   Lw
  //   Sw
  //   Addi
  //   Load_Byte
endmodule

module ALU_control (
  input  [1:0] ALUControl,
  input  [5:0] Funct,
  output [3:0] ALUOperation,
  output JR
);

  wire AllowedAdd, AllowedAnd, AllowedOr, AllowedSlt, AllowedSub, comparator_4_eq, comparator_5_eq,
       comparator_6_eq, comparator_7_eq, comparator_8_eq, comparator_9_eq, comparator_10_eq, EsResta, EsSuma,
       FunctionAllowed;

  Comparator #(.width(2)) comparator_1 (.a(2'b00), .b(ALUControl), .eq(EsSuma));  // open: gt, lt
  Comparator #(.width(2)) comparator_2 (.a(2'b01), .b(ALUControl), .eq(EsResta));  // open: gt, lt
  Comparator #(.width(2)) comparator_3 (.a(2'b10), .b(ALUControl), .eq(FunctionAllowed));  // open: gt, lt
  Comparator #(.width(6)) comparator_4 (.a(6'b100000), .b(Funct), .eq(comparator_4_eq));  // open: gt, lt
  Comparator #(.width(6)) comparator_5 (.a(6'b100010), .b(Funct), .eq(comparator_5_eq));  // open: gt, lt
  Comparator #(.width(6)) comparator_6 (.a(6'b100101), .b(Funct), .eq(comparator_6_eq));  // open: gt, lt
  Comparator #(.width(6)) comparator_7 (.a(6'b100111), .b(Funct), .eq(comparator_7_eq));  // open: gt, lt
  Comparator #(.width(6)) comparator_8 (.a(6'b101010), .b(Funct), .eq(comparator_8_eq));  // open: gt, lt
  Comparator #(.width(6)) comparator_9 (.a(6'b001000), .b(Funct), .eq(comparator_9_eq));  // open: gt, lt
  Comparator #(.width(6)) comparator_10 (.a(6'b100100), .b(Funct), .eq(comparator_10_eq));  // open: gt, lt
  and and_1 (AllowedAdd, comparator_4_eq, FunctionAllowed);
  and and_2 (AllowedSub, comparator_5_eq, FunctionAllowed);
  and and_3 (AllowedOr, comparator_6_eq, FunctionAllowed);
  and and_4 (ALUOperation[3], comparator_7_eq, FunctionAllowed);
  and and_5 (AllowedSlt, comparator_8_eq, FunctionAllowed);
  and and_6 (JR, comparator_9_eq, FunctionAllowed);
  and and_7 (AllowedAnd, comparator_10_eq, FunctionAllowed);
  or or_1 (ALUOperation[0], AllowedOr, AllowedSlt);
  or or_2 (ALUOperation[1], EsSuma, EsResta, AllowedAdd, AllowedSub, AllowedSlt);
  or or_3 (ALUOperation[2], EsResta, AllowedSub, AllowedSlt, ALUOperation[3]);

  // Other names for the same wires on the sheet: AllowedJr = JR; Bit0 = ALUOperation[0]; Bit1 = ALUOperation[1];
  //   Bit2 = ALUOperation[2]; AllowedNor = ALUOperation[3]; Bit3 = ALUOperation[3]; Funcion[5:0] = Funct

  // Notes on the sheet:
  //   EsTipoR
  //   EsSuma
  //   EsResta
  //   add
  //   sub
  //   or
  //   nor
  //   slt
  //   jr
  //   and
endmodule

module Main (
  input  clk,
  input  reset
);

  wire [5:0] funct, intruction_format_1_op_code;
  wire [31:0] fetch_instruction_1_instruction;

  Fetch_instruction fetch_instruction_1 (
    .CLK(clk), .reset(reset), .Instruction(fetch_instruction_1_instruction));  // open: next_PC, PCplus4
  intruction_format intruction_format_1 (
    .Instruction(fetch_instruction_1_instruction), .Op_code(intruction_format_1_op_code), .funct(funct));  // open: rs, rt, rd, shamt, inmediate, address
  controller controller_1 (.OpCode(intruction_format_1_op_code));  // open: ALUsource, RegDestino, Jump, Branch, MemRead, MemToReg, MemWrite, RegWrite, ALUoperation, LoadByte
  ALU_control alu_control_1 (.Funct(funct));  // open: ALUControl, ALUOperation, JR
endmodule

module Fetch_instruction (
  input  [31:0] next_PC,
  input  CLK,
  input  reset,
  output [31:0] PCplus4,
  output [31:0] Instruction
);

  wire [31:0] PC_q;

  Register #(.width(32)) PC (.D(next_PC), .en(1'b1), .clk(CLK), .Q(PC_q), .clr(reset));
  Adder #(.width(32)) adder_1 (.a(PC_q), .b(32'h4), .out(PCplus4), .cin(1'b0));  // open: cout
  ROM #(.dataWidth(32)) ROM_256_x_32_5232b435 (.addr(PC_q[9:2]), .data(Instruction));

  // Notes on the sheet:
  //   contents of ROM_256_x_32_5232b435 (hex, n*v repeats v):
  //   20080200 2009020a ad090000 81040000 20050100 c000012 20060300 acc20000 20050100 c000036 acc20004
  //   acc30008 8cd30000 8cd40004 8cd50008 20080120 8d160004 8000011 23bdfff4 afbf0008 afb10004 afb20000
  //   20110000 20120001 20080000 a05820 104482a 11200014 1100000a 200a0001 110a000c 2525020 1515020
  //   2408820 1409020 ad6a0000 216b0004 21080001 800001a ad600000 216b0004 21080001 800001a 200a0001
  //   ad6a0000 216b0004 21080001 800001a 2401020 8fbf0008 8fb10004 8fb20000 23bd000c 3e00008 23bdfffc
  //   afbf0000 20020000 20030000 20080000 a05820 104482a 11200006 816a0000 4a1020 20630001 216b0004
  //   21080001 800003c 8fbf0000 23bd0004 3e00008
endmodule

module mainIA (
  input  clk,
  input  reset
);

  wire ALUsource, Branch, JR, Jump, LoadByte, MemRead, MemToReg, MemWrite, NotJR, PCSrc, RegDestino,
       RegWrite, RegWriteEn, Zero;
  wire [1:0] ALUoperation_t;
  wire [3:0] ALUOperation;
  wire [4:0] rd, rs, rt, shamt, WriteReg;
  wire [5:0] funct, OpCode;
  wire [7:0] multiplexer_1_p6;
  wire [15:0] immediate;
  wire [25:0] address;
  wire [27:0] PCplus4;
  wire [31:0] ALUb, ALUresult, BranchTarget, ByteExt, Instruction, MemData, MemValue, nextPC, PCafterBranch,
       PCafterJump, ReadData1, ReadData2, WriteData;
  wire [31:2] ShiftedImm;
  wire [31:28] JumpTarget;
  wire [31:30] SignImm;

  assign {SignImm, ShiftedImm} = {{16{immediate[15]}}, immediate};  // Bit_Extender bit_extender_1
  Fetch_instruction fetch_instruction_1 (
    .next_PC(nextPC), .CLK(clk), .reset(reset), .PCplus4({JumpTarget, PCplus4}), .Instruction(Instruction));
  intruction_format intruction_format_1 (
    .Instruction(Instruction), .Op_code(OpCode), .rs(rs), .rt(rt), .rd(rd), .shamt(shamt), .funct(funct),
    .inmediate(immediate), .address(address));
  // Multiplexer #(.select(2), .width(8)) multiplexer_1: pin names not known; wires that end beside it: MemData[15:8], MemData[23:16], MemData[31:24], ALUresult[1:0], MemData[7:0], multiplexer_1_p6
  assign ByteExt = {{24{multiplexer_1_p6[7]}}, multiplexer_1_p6};  // Bit_Extender bit_extender_2
  not not_1 (NotJR, JR);
  and and_1 (PCSrc, Branch, Zero);
  controller controller_1 (
    .OpCode(OpCode), .ALUsource(ALUsource), .RegDestino(RegDestino), .Jump(Jump), .Branch(Branch),
    .MemRead(MemRead), .MemToReg(MemToReg), .MemWrite(MemWrite), .RegWrite(RegWrite),
    .ALUoperation(ALUoperation_t), .LoadByte(LoadByte));
  ALU_control alu_control_1 (.ALUControl(ALUoperation_t), .Funct(funct), .ALUOperation(ALUOperation), .JR(JR));
  Adder #(.width(32)) adder_1 (
    .a({JumpTarget, PCplus4}), .b({ShiftedImm, 2'b00}), .out(BranchTarget), .cin(1'b0));  // open: cout
  Multiplexer #(.width(32)) multiplexer_2 (.in0(MemData), .in1(ByteExt), .out(MemValue), .sel(LoadByte));
  and and_2 (RegWriteEn, NotJR, RegWrite);
  Multiplexer #(.width(32)) multiplexer_3 (
    .in0({JumpTarget, PCplus4}), .in1(BranchTarget), .out(PCafterBranch), .sel(PCSrc));
  Multiplexer #(.width(32)) multiplexer_4 (.in0(ALUresult), .in1(MemValue), .out(WriteData), .sel(MemToReg));
  Multiplexer #(.width(5)) multiplexer_5 (.in0(rt), .in1(rd), .out(WriteReg), .sel(RegDestino));
  Multiplexer #(.width(32)) multiplexer_6 (
    .in0(PCafterBranch), .in1({JumpTarget, address, 2'b00}), .out(PCafterJump), .sel(Jump));
  register_bank register_bank_1 (
    .Clock(clk), .Reset(reset), .Write_data(WriteData), .Bit_register_1(rs), .Bit_register_2(rt),
    .Write_register(WriteReg), .enable_write(RegWriteEn), .ReadData1(ReadData1), .ReadData2(ReadData2));
  ALU32bits alu32bits_1 (.B(ALUb), .A(ReadData1), .ALUOperation(ALUOperation), .ZERO(Zero), .out_5(ALUresult));
  Multiplexer #(.width(32)) multiplexer_7 (.in0(PCafterJump), .in1(ReadData1), .out(nextPC), .sel(JR));
  Multiplexer #(.width(32)) multiplexer_8 (.in0(ReadData2), .in1({SignImm, ShiftedImm}), .out(ALUb), .sel(ALUsource));
  DataMemory datamemory_1 (
    .Address(ALUresult), .mem_write(MemWrite), .mem_read(MemRead), .Clock_rate(clk),
    .Written_data(ReadData2), .Read_data(MemData));

  // Other names for the same wires on the sheet: JumpTarget[27:2] = address; PCplus4[31:28] = JumpTarget;
  //   SignImm[29:0] = ShiftedImm

  // Notes on the sheet:
  //   Inmediato, branch y salto
  //   Fetch
  //   Load byte y escritura
  //   Formato
  //   Siguiente PC
  //   Control
  //   Control ALU
  //   Registros
  //   ALU  (arriba ZERO, abajo resultado)
  //   Memoria
endmodule
