// Logisim project procesador_monociclo.circ as structural Verilog: 12 circuits, main circuit main
module alu32 (
  input  [31:0] A,
  input  [31:0] B,
  input  [2:0] ALUOperation,
  output [31:0] Result,
  output Zero
);

  wire comparator_1_lt;
  wire [31:0] adder_1_out, and_1_out, bit_extender_1_out, nor_1_out, or_1_out, subtractor_1_out;

  assign and_1_out = A & B;  // AND_Gate and_1, 32 bits wide
  assign or_1_out = A | B;  // OR_Gate or_1, 32 bits wide
  assign nor_1_out = ~(A | B);  // NOR_Gate nor_1, 32 bits wide
  Adder #(.width(32)) adder_1 (.a(A), .b(B), .out(adder_1_out));  // open: cin, cout
  Subtractor #(.width(32)) subtractor_1 (.a(A), .b(B), .out(subtractor_1_out));  // open: bin, bout
  Comparator #(.width(32), .mode("twosComplement")) comparator_1 (.a(A), .b(B), .lt(comparator_1_lt));  // open: gt, eq
  assign bit_extender_1_out = {{31{1'b0}}, comparator_1_lt};  // Bit_Extender bit_extender_1
  Multiplexer #(.select(3), .width(32)) multiplexer_1 (
    .in0(adder_1_out), .in1(subtractor_1_out), .in2(and_1_out), .in3(or_1_out), .in4(nor_1_out),
    .in5(bit_extender_1_out), .in6({32{1'b0}}), .in7({32{1'b0}}), .out(Result), .sel(ALUOperation));
  Comparator #(.width(32), .mode("unsigned")) comparator_2 (.a(Result), .b({32{1'b0}}), .eq(Zero));  // open: gt, lt
endmodule

module banco_registros (
  input  [4:0] ReadReg1,
  input  [4:0] ReadReg2,
  input  [4:0] WriteReg,
  input  [31:0] WriteData,
  input  RegWrite,
  input  CLK,
  input  Reset,
  output [31:0] ReadData1,
  output [31:0] ReadData2
);

  wire Decodificador_out1, Decodificador_out2, Decodificador_out3, Decodificador_out4, Decodificador_out5,
       Decodificador_out6, Decodificador_out7, Decodificador_out8, Decodificador_out9, Decodificador_out10,
       Decodificador_out11, Decodificador_out12, Decodificador_out13, Decodificador_out14,
       Decodificador_out15, Decodificador_out16, Decodificador_out17, Decodificador_out18,
       Decodificador_out19, Decodificador_out20, Decodificador_out21, Decodificador_out22,
       Decodificador_out23, Decodificador_out24, Decodificador_out25, Decodificador_out26,
       Decodificador_out27, Decodificador_out28, Decodificador_out29, Decodificador_out30,
       Decodificador_out31, undriven, undriven_2, undriven_3, undriven_4, undriven_5, undriven_6, undriven_7,
       undriven_8, undriven_9, undriven_10, undriven_11, undriven_12, undriven_13, undriven_14, undriven_15,
       undriven_16, undriven_17, undriven_18, undriven_19, undriven_20, undriven_21, undriven_22,
       undriven_23, undriven_24, undriven_25, undriven_26, undriven_27, undriven_28, undriven_29,
       undriven_30, undriven_31, undriven_32, undriven_33, undriven_34, undriven_35, undriven_36,
       undriven_37, undriven_38, undriven_39, undriven_40, undriven_41, undriven_42, undriven_43,
       undriven_44, undriven_45, undriven_46, undriven_47, undriven_48, undriven_49, undriven_50,
       undriven_51, undriven_52, undriven_53, undriven_54, undriven_55, undriven_56, undriven_57,
       undriven_58, undriven_59, undriven_60, undriven_61, undriven_62, undriven_63;
  wire [31:0] registro0_q, registro1_q, registro2_q, registro3_q, registro4_q, registro5_q, registro6_q,
       registro7_q, registro8_q, registro9_q, registro10_q, registro11_q, registro12_q, registro13_q,
       registro14_q, registro15_q, registro16_q, registro17_q, registro18_q, registro19_q, registro20_q,
       registro21_q, registro22_q, registro23_q, registro24_q, registro25_q, registro26_q, registro27_q,
       registro28_q, registro29_q, registro30_q, registro31_q, undriven_64, undriven_65, undriven_66,
       undriven_67, undriven_68, undriven_69, undriven_70, undriven_71, undriven_72, undriven_73,
       undriven_74, undriven_75, undriven_76, undriven_77, undriven_78, undriven_79, undriven_80,
       undriven_81, undriven_82, undriven_83, undriven_84, undriven_85, undriven_86, undriven_87,
       undriven_88, undriven_89, undriven_90, undriven_91, undriven_92, undriven_93, undriven_94,
       undriven_95, undriven_96, undriven_97, undriven_98, undriven_99, undriven_100, undriven_101,
       undriven_102, undriven_103, undriven_104, undriven_105, undriven_106, undriven_107, undriven_108,
       undriven_109, undriven_110, undriven_111, undriven_112, undriven_113, undriven_114, undriven_115,
       undriven_116, undriven_117, undriven_118, undriven_119, undriven_120, undriven_121, undriven_122,
       undriven_123, undriven_124, undriven_125, undriven_126, undriven_127, undriven_128, undriven_129,
       undriven_130, undriven_131, undriven_132, undriven_133, undriven_134, undriven_135, undriven_136,
       undriven_137, undriven_138, undriven_139, undriven_140, undriven_141, undriven_142, undriven_143,
       undriven_144, undriven_145, undriven_146;

  Decoder #(.select(5), .enable("true")) Decodificador (
    .out1(Decodificador_out1), .out2(Decodificador_out2), .out3(Decodificador_out3),
    .out4(Decodificador_out4), .out5(Decodificador_out5), .out6(Decodificador_out6),
    .out7(Decodificador_out7), .out8(Decodificador_out8), .out9(Decodificador_out9),
    .out10(Decodificador_out10), .out11(Decodificador_out11), .out12(Decodificador_out12),
    .out13(Decodificador_out13), .out14(Decodificador_out14), .out15(Decodificador_out15),
    .out16(Decodificador_out16), .out17(Decodificador_out17), .out18(Decodificador_out18),
    .out19(Decodificador_out19), .out20(Decodificador_out20), .out21(Decodificador_out21),
    .out22(Decodificador_out22), .out23(Decodificador_out23), .out24(Decodificador_out24),
    .out25(Decodificador_out25), .out26(Decodificador_out26), .out27(Decodificador_out27),
    .out28(Decodificador_out28), .out29(Decodificador_out29), .out30(Decodificador_out30),
    .out31(Decodificador_out31), .sel(WriteReg), .en(RegWrite));  // open: out0
  Register #(.width(32), .trigger("rising")) registro0 (
    .D({32{1'b0}}), .en(1'b1), .Q(registro0_q), .clk(undriven_33), .clr(undriven_2));
  Register #(.width(32), .trigger("rising")) registro1 (
    .D(undriven_64), .en(Decodificador_out1), .Q(registro1_q), .clk(undriven_34), .clr(undriven_3));
  Register #(.width(32), .trigger("rising")) registro2 (
    .D(undriven_65), .en(Decodificador_out2), .Q(registro2_q), .clk(undriven_35), .clr(undriven_4));
  Register #(.width(32), .trigger("rising")) registro3 (
    .D(undriven_66), .en(Decodificador_out3), .Q(registro3_q), .clk(undriven_36), .clr(undriven_5));
  Register #(.width(32), .trigger("rising")) registro4 (
    .D(undriven_67), .en(Decodificador_out4), .Q(registro4_q), .clk(undriven_37), .clr(undriven_6));
  Register #(.width(32), .trigger("rising")) registro5 (
    .D(undriven_68), .en(Decodificador_out5), .Q(registro5_q), .clk(undriven_38), .clr(undriven_7));
  Register #(.width(32), .trigger("rising")) registro6 (
    .D(undriven_69), .en(Decodificador_out6), .Q(registro6_q), .clk(undriven_39), .clr(undriven_8));
  Register #(.width(32), .trigger("rising")) registro7 (
    .D(undriven_70), .en(Decodificador_out7), .Q(registro7_q), .clk(undriven_40), .clr(undriven_9));
  Register #(.width(32), .trigger("rising")) registro8 (
    .D(undriven_71), .en(Decodificador_out8), .Q(registro8_q), .clk(undriven_41), .clr(undriven_10));
  Register #(.width(32), .trigger("rising")) registro9 (
    .D(undriven_72), .en(Decodificador_out9), .Q(registro9_q), .clk(undriven_42), .clr(undriven_11));
  Register #(.width(32), .trigger("rising")) registro10 (
    .D(undriven_73), .en(Decodificador_out10), .Q(registro10_q), .clk(undriven_43), .clr(undriven_12));
  Register #(.width(32), .trigger("rising")) registro11 (
    .D(undriven_74), .en(Decodificador_out11), .Q(registro11_q), .clk(undriven_44), .clr(undriven_13));
  Register #(.width(32), .trigger("rising")) registro12 (
    .D(undriven_75), .en(Decodificador_out12), .Q(registro12_q), .clk(undriven_45), .clr(undriven_14));
  Register #(.width(32), .trigger("rising")) registro13 (
    .D(undriven_76), .en(Decodificador_out13), .Q(registro13_q), .clk(undriven_46), .clr(undriven_15));
  Register #(.width(32), .trigger("rising")) registro14 (
    .D(undriven_77), .en(Decodificador_out14), .Q(registro14_q), .clk(undriven_47), .clr(undriven_16));
  Register #(.width(32), .trigger("rising")) registro15 (
    .D(undriven_78), .en(Decodificador_out15), .Q(registro15_q), .clk(undriven_48), .clr(undriven_17));
  Register #(.width(32), .trigger("rising")) registro16 (
    .D(undriven_79), .en(Decodificador_out16), .Q(registro16_q), .clk(undriven_49), .clr(undriven_18));
  Register #(.width(32), .trigger("rising")) registro17 (
    .D(undriven_80), .en(Decodificador_out17), .Q(registro17_q), .clk(undriven_50), .clr(undriven_19));
  Register #(.width(32), .trigger("rising")) registro18 (
    .D(undriven_81), .en(Decodificador_out18), .Q(registro18_q), .clk(undriven_51), .clr(undriven_20));
  Register #(.width(32), .trigger("rising")) registro19 (
    .D(undriven_82), .en(Decodificador_out19), .Q(registro19_q), .clk(undriven_52), .clr(undriven_21));
  Register #(.width(32), .trigger("rising")) registro20 (
    .D(undriven_83), .en(Decodificador_out20), .Q(registro20_q), .clk(undriven_53), .clr(undriven_22));
  Register #(.width(32), .trigger("rising")) registro21 (
    .D(undriven_84), .en(Decodificador_out21), .Q(registro21_q), .clk(undriven_54), .clr(undriven_23));
  Register #(.width(32), .trigger("rising")) registro22 (
    .D(undriven_85), .en(Decodificador_out22), .Q(registro22_q), .clk(undriven_55), .clr(undriven_24));
  Register #(.width(32), .trigger("rising")) registro23 (
    .D(undriven_86), .en(Decodificador_out23), .Q(registro23_q), .clk(undriven_56), .clr(undriven_25));
  Register #(.width(32), .trigger("rising")) registro24 (
    .D(undriven_87), .en(Decodificador_out24), .Q(registro24_q), .clk(undriven_57), .clr(undriven_26));
  Register #(.width(32), .trigger("rising")) registro25 (
    .D(undriven_88), .en(Decodificador_out25), .Q(registro25_q), .clk(undriven_58), .clr(undriven_27));
  Register #(.width(32), .trigger("rising")) registro26 (
    .D(undriven_89), .en(Decodificador_out26), .Q(registro26_q), .clk(undriven_59), .clr(undriven_28));
  Register #(.width(32), .trigger("rising")) registro27 (
    .D(undriven_90), .en(Decodificador_out27), .Q(registro27_q), .clk(undriven_60), .clr(undriven_29));
  Register #(.width(32), .trigger("rising")) registro28 (
    .D(undriven_91), .en(Decodificador_out28), .Q(registro28_q), .clk(undriven_61), .clr(undriven_30));
  Register #(.width(32), .trigger("rising")) registro29 (
    .D(undriven_92), .en(Decodificador_out29), .Q(registro29_q), .clk(undriven_62), .clr(undriven_31));
  Register #(.width(32), .trigger("rising")) registro30 (
    .D(undriven_93), .en(Decodificador_out30), .Q(registro30_q), .clk(undriven_63), .clr(undriven_32));
  Register #(.width(32), .trigger("rising")) registro31 (
    .D(WriteData), .en(Decodificador_out31), .Q(registro31_q), .clk(undriven_33), .clr(undriven));
  Multiplexer #(.select(5), .width(32)) Mux_A_rs (
    .in0(undriven_146), .in1(undriven_145), .in2(undriven_144), .in3(undriven_143), .in4(undriven_142),
    .in5(undriven_141), .in6(undriven_140), .in7(undriven_139), .in8(undriven_138), .in9(undriven_137),
    .in10(undriven_136), .in11(undriven_135), .in12(undriven_133), .in13(undriven_127), .in14(undriven_129),
    .in15(undriven_123), .in16(undriven_121), .in17(undriven_119), .in18(undriven_117), .in19(undriven_115),
    .in20(undriven_131), .in21(undriven_113), .in22(undriven_111), .in23(undriven_104), .in24(undriven_106),
    .in25(undriven_102), .in26(undriven_124), .in27(undriven_100), .in28(undriven_98), .in29(undriven_96),
    .in30(undriven_108), .in31(undriven_94), .out(ReadData1), .sel(ReadReg1));
  Multiplexer #(.select(5), .width(32)) Mux_B_rt (
    .in0(registro0_q), .in1(registro1_q), .in2(registro2_q), .in3(registro3_q), .in4(registro4_q),
    .in5(registro5_q), .in6(registro6_q), .in7(registro7_q), .in8(registro8_q), .in9(registro9_q),
    .in10(registro10_q), .in11(undriven_134), .in12(undriven_132), .in13(undriven_126), .in14(undriven_128),
    .in15(undriven_122), .in16(undriven_120), .in17(undriven_118), .in18(undriven_116), .in19(undriven_114),
    .in20(undriven_130), .in21(undriven_112), .in22(undriven_110), .in23(undriven_105), .in24(undriven_107),
    .in25(undriven_103), .in26(undriven_125), .in27(undriven_101), .in28(undriven_99), .in29(undriven_97),
    .in30(undriven_109), .in31(undriven_95), .out(ReadData2), .sel(ReadReg2));
endmodule

module isplit (
  input  [31:0] Instruction,
  output [5:0] opcode,
  output [4:0] rs,
  output [4:0] rt,
  output [4:0] rd,
  output [4:0] shamt,
  output [5:0] funct,
  output [15:0] imm,
  output [25:0] target
);


  assign funct = Instruction[5:0];
  assign imm = Instruction[15:0];
  assign opcode = Instruction[31:26];
  assign rd = Instruction[15:11];
  assign rs = Instruction[25:21];
  assign rt = Instruction[20:16];
  assign shamt = Instruction[10:6];
  assign target = Instruction[25:0];
endmodule

module fetch (
  input  [31:0] nextPC,
  input  CLK,
  input  reset,
  output [31:0] PC,
  output [31:0] PCplus4,
  output [31:0] Instruction
);

  Register #(.width(32), .trigger("rising")) Registro_PC (.D(nextPC), .en(1'b1), .Q(PC), .clk(CLK), .clr(reset));
  Adder #(.width(32)) Sumador_PC4 (.a(PC), .b(32'h4), .out(PCplus4), .cin(1'b0));  // open: cout
  ROM #(.addrWidth(12), .dataWidth(32)) rom_1 (.addr(PC[11:0]), .data(Instruction));

  // Notes on the sheet:
  //   contents of rom_1 (hex, n*v repeats v):
  //   20080200 0 0 0 2009020a 0 0 0 ad090000 0 0 0 81040000 0 0 0 20050100 0 0 0 c000012 0 0 0 20060300 0
  //   0 0 acc20000 0 0 0 20050100 0 0 0 c000036 0 0 0 acc20004 0 0 0 acc30008 0 0 0 8cd30000 0 0 0
  //   8cd40004 0 0 0 8cd50008 0 0 0 20080120 0 0 0 8d160004 0 0 0 8000011 0 0 0 23bdfff4 0 0 0 afbf0008 0
  //   0 0 afb10004 0 0 0 afb20000 0 0 0 20110000 0 0 0 20120001 0 0 0 20080000 0 0 0 a05820 0 0 0 104482a
  //   0 0 0 11200014 0 0 0 1100000a 0 0 0 200a0001 0 0 0 110a000c 0 0 0 2525020 0 0 0 1515020 0 0 0
  //   2408820 0 0 0 1409020 0 0 0 ad6a0000 0 0 0 216b0004 0 0 0 21080001 0 0 0 800001a 0 0 0 ad600000 0 0
  //   0 216b0004 0 0 0 21080001 0 0 0 800001a 0 0 0 200a0001 0 0 0 ad6a0000 0 0 0 216b0004 0 0 0 21080001
  //   0 0 0 800001a 0 0 0 2401020 0 0 0 8fbf0008 0 0 0 8fb10004 0 0 0 8fb20000 0 0 0 23bd000c 0 0 0
  //   3e00008 0 0 0 23bdfffc 0 0 0 afbf0000 0 0 0 20020000 0 0 0 20030000 0 0 0 20080000 0 0 0 a05820 0 0
  //   0 104482a 0 0 0 11200006 0 0 0 816a0000 0 0 0 4a1020 0 0 0 20630001 0 0 0 216b0004 0 0 0 21080001 0
  //   0 0 800003c 0 0 0 8fbf0000 0 0 0 23bd0004 0 0 0 3e00008 3815*0
endmodule

module unidad_control (
  input  [5:0] opcode,
  input  [5:0] funct,
  output RegWrite,
  output MemRead,
  output MemWrite,
  output Branch,
  output ALUSrc,
  output [1:0] wr_sel,
  output [1:0] mtr_sel,
  output [1:0] pc_sel,
  output [1:0] ALUOp
);

  wire [15:13] ROM_control_data;

  ROM #(.addrWidth(12), .dataWidth(16)) ROM_control (
    .addr({opcode, funct}),
    .data({ROM_control_data, ALUOp, pc_sel[1], wr_sel[1], pc_sel[0], Branch, MemWrite, MemRead, RegWrite, mtr_sel, ALUSrc, wr_sel[0]}));

  // Notes on the sheet:
  //   contents of ROM_control (hex, n*v repeats v):
  //   8*1011 400 55*1011 64*0 64*100 64*31c 64*880 192*0 64*12 1472*0 64*3a 128*0 64*36 448*0 64*42 1280*0
endmodule

module control_alu (
  input  [1:0] ALUOp,
  input  [5:0] funct,
  output [2:0] op
);

  ROM #(.addrWidth(8), .dataWidth(3)) ROM_control_ALU (.addr({ALUOp, funct}), .data(op));

  // Notes on the sheet:
  //   contents of ROM_control_ALU (hex, n*v repeats v):
  //   64*0 64*1 34*0 1 0 2 3 0 4 0 0 5 85*0
endmodule

module mem_datos (
  input  [31:0] Address,
  input  [31:0] WriteData,
  input  MemWrite,
  input  MemRead,
  input  CLK,
  output [31:0] ReadData,
  output [31:0] ReadDataByte
);

  wire [7:0] bitselector_1_out;

  RAM #(.addrWidth(12), .dataWidth(32), .enables("byte"), .databus("bibus"), .asyncread("true"), .trigger("rising"), .byteenables("NobyteEnables"), .\type ("volatile"), .clearpin("false"), .line("single"), .misaligned("false")) Memoria_datos (
    .addr(Address[13:2]), .we(MemWrite), .oe(MemRead), .clk(CLK), .din(WriteData), .dout(ReadData));
  BitSelector #(.width(32), .group(8)) bitselector_1 (.in(ReadData), .out(bitselector_1_out), .sel(Address[1:0]));
  assign ReadDataByte = {{24{bitselector_1_out[7]}}, bitselector_1_out};  // Bit_Extender Extension_LB
endmodule

module proximo_pc (
  input  [31:0] pc4,
  input  [15:0] imm,
  input  [25:0] target,
  input  [31:0] a_val,
  input  Branch,
  input  zero_flag,
  input  [1:0] pc_sel,
  output [31:0] pc_next
);

  wire Branch_and_Zero_out;
  wire [31:0] and_1_out, bit_extender_1_out, Extension_inmediato_out, offset_shift2_out, or_1_out,
       PC_offset_out, secuencial_branch_out, shifter_1_out;

  assign Extension_inmediato_out = {{16{imm[15]}}, imm};  // Bit_Extender Extension_inmediato
  Shifter #(.width(32), .shift("ll")) offset_shift2 (
    .in(Extension_inmediato_out), .\dist (5'b00010), .out(offset_shift2_out));
  and Branch_and_Zero (Branch_and_Zero_out, Branch, zero_flag);
  assign bit_extender_1_out = {{6{1'b0}}, target};  // Bit_Extender bit_extender_1
  Adder #(.width(32)) PC_offset (.a(pc4), .b(offset_shift2_out), .out(PC_offset_out), .cin(1'b0));  // open: cout
  Shifter #(.width(32), .shift("ll")) shifter_1 (.in(bit_extender_1_out), .\dist (5'b00010), .out(shifter_1_out));
  Multiplexer #(.select(1), .width(32)) secuencial_branch (
    .in0(pc4), .in1(PC_offset_out), .out(secuencial_branch_out), .sel(Branch_and_Zero_out));
  assign and_1_out = pc4 & 32'hf0000000;  // AND_Gate and_1, 32 bits wide
  assign or_1_out = shifter_1_out | and_1_out;  // OR_Gate or_1, 32 bits wide
  Multiplexer #(.select(2), .width(32)) Proximo_PC (
    .in0(secuencial_branch_out), .in1(or_1_out), .in2(a_val), .in3(a_val), .out(pc_next), .sel(pc_sel));
endmodule

module write_reg (
  input  [4:0] rt,
  input  [4:0] rd,
  input  [1:0] wr_sel,
  output [4:0] wr
);

  Multiplexer #(.select(2), .width(5)) Mux_RegDst (
    .in0(rt), .in1(rd), .in2({5{1'b1}}), .in3({5{1'b1}}), .out(wr), .sel(wr_sel));
endmodule

module writeback (
  input  [31:0] alu_res,
  input  [31:0] mem_rdata,
  input  [31:0] lb_val,
  input  [31:0] pc4,
  input  [1:0] sel,
  output [31:0] wr_data
);

  Multiplexer #(.select(2), .width(32)) Mux_MemtoReg (
    .in0(alu_res), .in1(mem_rdata), .in2(lb_val), .in3(pc4), .out(wr_data), .sel(sel));
endmodule

module alu (
  input  [31:0] A,
  input  [31:0] B,
  input  [15:0] imm,
  input  ALUSrc,
  input  [2:0] ALUOperation,
  output [31:0] Result,
  output Zero
);

  wire [31:0] Extension_inmediato_out, Mux_ALUSrc_out;

  assign Extension_inmediato_out = {{16{imm[15]}}, imm};  // Bit_Extender Extension_inmediato
  Multiplexer #(.select(1), .width(32)) Mux_ALUSrc (
    .in0(B), .in1(Extension_inmediato_out), .out(Mux_ALUSrc_out), .sel(ALUSrc));
  alu32 alu32_1 (.A(A), .B(Mux_ALUSrc_out), .ALUOperation(ALUOperation), .Result(Result), .Zero(Zero));
endmodule

module main (
  input  RST
);

  wire alu_1_zero, banco_registros_1_p6, banco_registros_1_p7, clock_1_out, unidad_control_1_p3,
       unidad_control_1_p4, unidad_control_1_p5, unidad_control_1_p6, unidad_control_1_p7;
  wire [1:0] unidad_control_1_p8, unidad_control_1_p9, unidad_control_1_p10, unidad_control_1_p11;
  wire [2:0] control_alu_1_op;
  wire [4:0] isplit_1_rd, isplit_1_rs, isplit_1_rt, undriven_2, write_reg_1_wr;
  wire [5:0] isplit_1_funct, isplit_1_opcode, undriven;
  wire [15:0] isplit_1_imm;
  wire [25:0] isplit_1_target;
  wire [31:0] alu_1_result, banco_registros_1_p4, banco_registros_1_p8, banco_registros_1_p9,
       fetch_1_instruction, fetch_1_pcplus4, mem_datos_1_readdata, mem_datos_1_readdatabyte,
       proximo_pc_1_pc_next, undriven_3, undriven_4, undriven_5;

  Clock clock_1 (.out(clock_1_out));
  fetch fetch_1 (
    .nextPC(proximo_pc_1_pc_next), .CLK(clock_1_out), .reset(RST), .PCplus4(fetch_1_pcplus4),
    .Instruction(fetch_1_instruction));  // open: PC
  proximo_pc proximo_pc_1 (
    .pc4(fetch_1_pcplus4), .imm(isplit_1_imm), .target(isplit_1_target), .a_val(undriven_3),
    .Branch(unidad_control_1_p6), .zero_flag(alu_1_zero), .pc_sel(unidad_control_1_p10),
    .pc_next(proximo_pc_1_pc_next));
  isplit isplit_1 (
    .Instruction(fetch_1_instruction), .opcode(isplit_1_opcode), .rs(isplit_1_rs), .rt(isplit_1_rt),
    .rd(isplit_1_rd), .funct(isplit_1_funct), .imm(isplit_1_imm), .target(isplit_1_target));  // open: shamt
  // unidad_control unidad_control_1: pin names not known; wires that end beside it: isplit_1_opcode, isplit_1_funct, unidad_control_1_p3, unidad_control_1_p4, unidad_control_1_p5, unidad_control_1_p6, unidad_control_1_p7, unidad_control_1_p8, unidad_control_1_p9, unidad_control_1_p10, unidad_control_1_p11
  write_reg write_reg_1 (.rt(undriven_2), .rd(isplit_1_rd), .wr_sel(unidad_control_1_p8), .wr(write_reg_1_wr));
  // banco_registros banco_registros_1: pin names not known; wires that end beside it: isplit_1_rs, isplit_1_rt, write_reg_1_wr, banco_registros_1_p4, unidad_control_1_p3, banco_registros_1_p6, banco_registros_1_p7, banco_registros_1_p8, banco_registros_1_p9
  control_alu control_alu_1 (.ALUOp(unidad_control_1_p11), .funct(undriven), .op(control_alu_1_op));
  alu alu_1 (
    .A(banco_registros_1_p8), .B(banco_registros_1_p9), .imm(isplit_1_imm), .ALUSrc(unidad_control_1_p7),
    .ALUOperation(control_alu_1_op), .Result(alu_1_result), .Zero(alu_1_zero));
  writeback writeback_1 (
    .alu_res(undriven_5), .mem_rdata(mem_datos_1_readdata), .lb_val(mem_datos_1_readdatabyte),
    .pc4(fetch_1_pcplus4), .sel(unidad_control_1_p9), .wr_data(banco_registros_1_p4));
  mem_datos mem_datos_1 (
    .Address(alu_1_result), .WriteData(undriven_4), .MemWrite(unidad_control_1_p5),
    .MemRead(unidad_control_1_p4), .CLK(banco_registros_1_p6), .ReadData(mem_datos_1_readdata),
    .ReadDataByte(mem_datos_1_readdatabyte));
endmodule
